// Logisim project Death_Machine.circ as structural Verilog: 9 circuits, main circuit main
module main (
  output [15:0] out_1,
  output [15:0] out_2,
  output [23:0] INSTR
);

  wire alu_1_z, control_unit_1_alusrc, control_unit_1_cbr, control_unit_1_linkreg, control_unit_1_memtoreg,
       control_unit_1_memwrite, control_unit_1_pbr, control_unit_1_reg2loc, control_unit_1_regwrite,
       control_unit_1_ubr, MEM_CLOCK_out, SYS_CLOCK_out;
  wire [2:0] multiplexer_1_out;
  wire [7:0] hex_to_led_1_led_1, hex_to_led_1_led_1_2, hex_to_led_1_led_1_3, hex_to_led_1_led_1_4,
       hex_to_led_1_led_2, hex_to_led_1_led_2_2, hex_to_led_1_led_2_3, hex_to_led_1_led_2_4,
       hex_to_led_1_led_3, hex_to_led_1_led_3_2, hex_to_led_1_led_3_3, hex_to_led_1_led_3_4,
       hex_to_led_1_led_4, hex_to_led_1_led_4_2, hex_to_led_1_led_4_3, hex_to_led_1_led_4_4,
       hex_to_led_2_led_1, hex_to_led_2_led_1_2, hex_to_led_2_led_1_3, hex_to_led_2_led_1_4,
       hex_to_led_2_led_2, hex_to_led_2_led_2_2, hex_to_led_2_led_2_3, hex_to_led_2_led_2_4,
       hex_to_led_2_led_3, hex_to_led_2_led_3_2, hex_to_led_2_led_3_3, hex_to_led_2_led_3_4,
       hex_to_led_2_led_4, hex_to_led_2_led_4_2, hex_to_led_2_led_4_3, hex_to_led_2_led_4_4,
       hex_to_led_3_led_1, hex_to_led_3_led_1_2, hex_to_led_3_led_1_3, hex_to_led_3_led_1_4,
       hex_to_led_3_led_2, hex_to_led_3_led_2_2, hex_to_led_3_led_2_3, hex_to_led_3_led_2_4,
       hex_to_led_3_led_3, hex_to_led_3_led_3_2, hex_to_led_3_led_3_3, hex_to_led_3_led_3_4,
       hex_to_led_3_led_4, hex_to_led_3_led_4_2, hex_to_led_3_led_4_3, hex_to_led_3_led_4_4,
       hex_to_led_4_led_1, hex_to_led_4_led_1_2, hex_to_led_4_led_1_3, hex_to_led_4_led_1_4,
       hex_to_led_4_led_2, hex_to_led_4_led_2_2, hex_to_led_4_led_2_3, hex_to_led_4_led_2_4,
       hex_to_led_4_led_3, hex_to_led_4_led_3_2, hex_to_led_4_led_3_3, hex_to_led_4_led_3_4,
       hex_to_led_4_led_4, hex_to_led_4_led_4_2, hex_to_led_4_led_4_3, hex_to_led_4_led_4_4,
       hex_to_led_5_led_1, hex_to_led_5_led_1_2, hex_to_led_5_led_1_3, hex_to_led_5_led_1_4,
       hex_to_led_5_led_2, hex_to_led_5_led_2_2, hex_to_led_5_led_2_3, hex_to_led_5_led_2_4,
       hex_to_led_5_led_4, hex_to_led_5_led_4_2, hex_to_led_5_led_4_3, hex_to_led_5_led_4_4,
       hex_to_led_6_led_1, hex_to_led_6_led_1_2, hex_to_led_6_led_1_3, hex_to_led_6_led_1_4,
       hex_to_led_6_led_2, hex_to_led_6_led_2_2, hex_to_led_6_led_2_3, hex_to_led_6_led_2_4,
       hex_to_led_6_led_3, hex_to_led_6_led_3_2, hex_to_led_6_led_3_3, hex_to_led_6_led_3_4,
       hex_to_led_6_led_4, hex_to_led_6_led_4_2, hex_to_led_6_led_4_3, hex_to_led_6_led_4_4,
       hex_to_led_7_led_1, hex_to_led_7_led_1_2, hex_to_led_7_led_1_3, hex_to_led_7_led_1_4,
       hex_to_led_7_led_2, hex_to_led_7_led_2_2, hex_to_led_7_led_2_3, hex_to_led_7_led_2_4,
       hex_to_led_7_led_3, hex_to_led_7_led_3_2, hex_to_led_7_led_3_3, hex_to_led_7_led_3_4,
       hex_to_led_7_led_4, hex_to_led_7_led_4_2, hex_to_led_7_led_4_3, hex_to_led_7_led_4_4,
       hex_to_led_8_led_1, hex_to_led_8_led_1_2, hex_to_led_8_led_1_3, hex_to_led_8_led_1_4,
       hex_to_led_8_led_2, hex_to_led_8_led_2_2, hex_to_led_8_led_2_3, hex_to_led_8_led_2_4,
       hex_to_led_8_led_3, hex_to_led_8_led_3_2, hex_to_led_8_led_3_3, hex_to_led_8_led_3_4,
       hex_to_led_8_led_4, hex_to_led_8_led_4_2, hex_to_led_8_led_4_3, hex_to_led_8_led_4_4,
       hex_to_led_9_led_1, hex_to_led_9_led_1_2, hex_to_led_9_led_1_3, hex_to_led_9_led_1_4,
       hex_to_led_9_led_2, hex_to_led_9_led_2_2, hex_to_led_9_led_2_3, hex_to_led_9_led_2_4,
       hex_to_led_9_led_3, hex_to_led_9_led_3_2, hex_to_led_9_led_3_3, hex_to_led_9_led_3_4,
       hex_to_led_9_led_4, hex_to_led_9_led_4_2, hex_to_led_9_led_4_3, hex_to_led_9_led_4_4,
       instr_led_1_letter_1, instr_led_1_letter_1_2, instr_led_1_letter_1_3, instr_led_1_letter_1_4,
       instr_led_1_letter_2, instr_led_1_letter_2_2, instr_led_1_letter_2_3, instr_led_1_letter_2_4,
       instr_led_1_letter_3, instr_led_1_letter_3_2, instr_led_1_letter_3_3, instr_led_1_letter_3_4,
       instr_led_1_letter_4, instr_led_1_letter_4_2, instr_led_1_letter_4_3, instr_led_1_letter_4_4;
  wire [15:0] adder_1_out, alu_1_aluout, bit_extender_1_out, DATA_MEMORY_dout, multiplexer_2_out,
       multiplexer_3_out, PC_q, register_file_1_lr, register_file_1_regdata1, register_file_1_regdata2,
       register_file_1_x0, register_file_1_x1, register_file_1_x2, register_file_1_x3, register_file_1_x4,
       register_file_1_x5, register_file_1_xzr;
  wire [31:0] hex_to_led_5_led_3;

  DotMatrix #(.matrixcols(36), .matrixrows(8)) dotmatrix_1 (
    .col0(8'h42), .col1(8'h24), .col2(8'h18), .col3(8'h24), .col4(8'h42), .col5({8{1'b0}}), .col6(8'h7e),
    .col7(8'h42), .col8(8'h42), .col9(8'h7e), .col10({8{1'b0}}), .col11(8'h24), .col12(8'h24), .col13(8'h24),
    .col14(8'h24), .col15(8'h24), .col16({8{1'b0}}), .col17(hex_to_led_1_led_1_4),
    .col18(hex_to_led_1_led_1_3), .col19(hex_to_led_1_led_1_2), .col20(hex_to_led_1_led_1),
    .col21({8{1'b0}}), .col22(hex_to_led_1_led_2_4), .col23(hex_to_led_1_led_2_3),
    .col24(hex_to_led_1_led_2_2), .col25(hex_to_led_1_led_2), .col26({8{1'b0}}),
    .col27(hex_to_led_1_led_3_4), .col28(hex_to_led_1_led_3_3), .col29(hex_to_led_1_led_3_2),
    .col30(hex_to_led_1_led_3), .col31({8{1'b0}}), .col32(hex_to_led_1_led_4_4),
    .col33(hex_to_led_1_led_4_3), .col34(hex_to_led_1_led_4_2), .col35(hex_to_led_1_led_4));
  DotMatrix #(.matrixcols(36), .matrixrows(8)) dotmatrix_2 (
    .col0(8'h42), .col1(8'h24), .col2(8'h18), .col3(8'h24), .col4(8'h42), .col5({8{1'b0}}), .col6({8{1'b0}}),
    .col7(8'h7e), .col8({8{1'b0}}), .col9({8{1'b0}}), .col10({8{1'b0}}), .col11(8'h24), .col12(8'h24),
    .col13(8'h24), .col14(8'h24), .col15(8'h24), .col16({8{1'b0}}), .col17(hex_to_led_2_led_1_4),
    .col18(hex_to_led_2_led_1_3), .col19(hex_to_led_2_led_1_2), .col20(hex_to_led_2_led_1),
    .col21({8{1'b0}}), .col22(hex_to_led_2_led_2_4), .col23(hex_to_led_2_led_2_3),
    .col24(hex_to_led_2_led_2_2), .col25(hex_to_led_2_led_2), .col26({8{1'b0}}),
    .col27(hex_to_led_2_led_3_4), .col28(hex_to_led_2_led_3_3), .col29(hex_to_led_2_led_3_2),
    .col30(hex_to_led_2_led_3), .col31({8{1'b0}}), .col32(hex_to_led_2_led_4_4),
    .col33(hex_to_led_2_led_4_3), .col34(hex_to_led_2_led_4_2), .col35(hex_to_led_2_led_4));
  DotMatrix #(.matrixcols(36), .matrixrows(8)) dotmatrix_3 (
    .col0(8'h42), .col1(8'h24), .col2(8'h18), .col3(8'h24), .col4(8'h42), .col5({8{1'b0}}), .col6(8'h4e),
    .col7(8'h4a), .col8(8'h4a), .col9(8'h7a), .col10({8{1'b0}}), .col11(8'h24), .col12(8'h24), .col13(8'h24),
    .col14(8'h24), .col15(8'h24), .col16({8{1'b0}}), .col17(hex_to_led_3_led_1_4),
    .col18(hex_to_led_3_led_1_3), .col19(hex_to_led_3_led_1_2), .col20(hex_to_led_3_led_1),
    .col21({8{1'b0}}), .col22(hex_to_led_3_led_2_4), .col23(hex_to_led_3_led_2_3),
    .col24(hex_to_led_3_led_2_2), .col25(hex_to_led_3_led_2), .col26({8{1'b0}}),
    .col27(hex_to_led_3_led_3_4), .col28(hex_to_led_3_led_3_3), .col29(hex_to_led_3_led_3_2),
    .col30(hex_to_led_3_led_3), .col31({8{1'b0}}), .col32(hex_to_led_3_led_4_4),
    .col33(hex_to_led_3_led_4_3), .col34(hex_to_led_3_led_4_2), .col35(hex_to_led_3_led_4));
  DotMatrix #(.matrixcols(36), .matrixrows(8)) dotmatrix_4 (
    .col0(8'h42), .col1(8'h24), .col2(8'h18), .col3(8'h24), .col4(8'h42), .col5({8{1'b0}}), .col6(8'h4a),
    .col7(8'h4a), .col8(8'h4a), .col9(8'h7e), .col10({8{1'b0}}), .col11(8'h24), .col12(8'h24), .col13(8'h24),
    .col14(8'h24), .col15(8'h24), .col16({8{1'b0}}), .col17(hex_to_led_4_led_1_4),
    .col18(hex_to_led_4_led_1_3), .col19(hex_to_led_4_led_1_2), .col20(hex_to_led_4_led_1),
    .col21({8{1'b0}}), .col22(hex_to_led_4_led_2_4), .col23(hex_to_led_4_led_2_3),
    .col24(hex_to_led_4_led_2_2), .col25(hex_to_led_4_led_2), .col26({8{1'b0}}),
    .col27(hex_to_led_4_led_3_4), .col28(hex_to_led_4_led_3_3), .col29(hex_to_led_4_led_3_2),
    .col30(hex_to_led_4_led_3), .col31({8{1'b0}}), .col32(hex_to_led_4_led_4_4),
    .col33(hex_to_led_4_led_4_3), .col34(hex_to_led_4_led_4_2), .col35(hex_to_led_4_led_4));
  Register #(.width(16)) PC (.D(out_1), .en(1'b1), .clk(SYS_CLOCK_out), .Q(PC_q));  // open: clr
  Clock #(.highDuration(2), .lowDuration(2)) SYS_CLOCK (.out(SYS_CLOCK_out));
  RAM #(.addrWidth(16), .dataWidth(24), .enables("line"), .\type ("nonvolatile")) INSTRUCTION_MEMORY (
    .addr(PC_q), .we(1'b0), .clk(SYS_CLOCK_out), .dout(INSTR));  // open: din
  hex_to_LED hex_to_led_1 (
    .HEX_DIGIT(register_file_1_x0),
    .LED_4({hex_to_led_1_led_4_4, hex_to_led_1_led_4_3, hex_to_led_1_led_4_2, hex_to_led_1_led_4}),
    .LED_1({hex_to_led_1_led_1_4, hex_to_led_1_led_1_3, hex_to_led_1_led_1_2, hex_to_led_1_led_1}),
    .LED_2({hex_to_led_1_led_2_4, hex_to_led_1_led_2_3, hex_to_led_1_led_2_2, hex_to_led_1_led_2}),
    .LED_3({hex_to_led_1_led_3_4, hex_to_led_1_led_3_3, hex_to_led_1_led_3_2, hex_to_led_1_led_3}));
  hex_to_LED hex_to_led_2 (
    .HEX_DIGIT(register_file_1_x1),
    .LED_4({hex_to_led_2_led_4_4, hex_to_led_2_led_4_3, hex_to_led_2_led_4_2, hex_to_led_2_led_4}),
    .LED_1({hex_to_led_2_led_1_4, hex_to_led_2_led_1_3, hex_to_led_2_led_1_2, hex_to_led_2_led_1}),
    .LED_2({hex_to_led_2_led_2_4, hex_to_led_2_led_2_3, hex_to_led_2_led_2_2, hex_to_led_2_led_2}),
    .LED_3({hex_to_led_2_led_3_4, hex_to_led_2_led_3_3, hex_to_led_2_led_3_2, hex_to_led_2_led_3}));
  hex_to_LED hex_to_led_3 (
    .HEX_DIGIT(register_file_1_x2),
    .LED_4({hex_to_led_3_led_4_4, hex_to_led_3_led_4_3, hex_to_led_3_led_4_2, hex_to_led_3_led_4}),
    .LED_1({hex_to_led_3_led_1_4, hex_to_led_3_led_1_3, hex_to_led_3_led_1_2, hex_to_led_3_led_1}),
    .LED_2({hex_to_led_3_led_2_4, hex_to_led_3_led_2_3, hex_to_led_3_led_2_2, hex_to_led_3_led_2}),
    .LED_3({hex_to_led_3_led_3_4, hex_to_led_3_led_3_3, hex_to_led_3_led_3_2, hex_to_led_3_led_3}));
  hex_to_LED hex_to_led_4 (
    .HEX_DIGIT(register_file_1_x3),
    .LED_4({hex_to_led_4_led_4_4, hex_to_led_4_led_4_3, hex_to_led_4_led_4_2, hex_to_led_4_led_4}),
    .LED_1({hex_to_led_4_led_1_4, hex_to_led_4_led_1_3, hex_to_led_4_led_1_2, hex_to_led_4_led_1}),
    .LED_2({hex_to_led_4_led_2_4, hex_to_led_4_led_2_3, hex_to_led_4_led_2_2, hex_to_led_4_led_2}),
    .LED_3({hex_to_led_4_led_3_4, hex_to_led_4_led_3_3, hex_to_led_4_led_3_2, hex_to_led_4_led_3}));
  control_unit control_unit_1 (
    .OPCODE(INSTR[23:21]), .Reg2Loc(control_unit_1_reg2loc), .RegWrite(control_unit_1_regwrite),
    .MemToReg(control_unit_1_memtoreg), .MemWrite(control_unit_1_memwrite), .ALUsrc(control_unit_1_alusrc),
    .PBr(control_unit_1_pbr), .CBr(control_unit_1_cbr), .UBr(control_unit_1_ubr),
    .LinkReg(control_unit_1_linkreg));
  DotMatrix #(.matrixcols(34), .matrixrows(8)) dotmatrix_5 (
    .col0(8'h7e), .col1(8'h50), .col2(8'h50), .col3(8'h70), .col4({8{1'b0}}), .col5(8'h7e), .col6(8'h42),
    .col7(8'h42), .col8(8'h42), .col9({8{1'b0}}), .col10(8'h24), .col11(8'h24), .col12(8'h24), .col13(8'h24),
    .col14({8{1'b0}}), .col15(hex_to_led_5_led_1_4), .col16(hex_to_led_5_led_1_3),
    .col17(hex_to_led_5_led_1_2), .col18(hex_to_led_5_led_1), .col19({8{1'b0}}),
    .col20(hex_to_led_5_led_2_4), .col21(hex_to_led_5_led_2_3), .col22(hex_to_led_5_led_2_2),
    .col23(hex_to_led_5_led_2), .col24({8{1'b0}}), .col25(hex_to_led_5_led_3[31:24]),
    .col26(hex_to_led_5_led_3[23:16]), .col27(hex_to_led_5_led_3[15:8]), .col28(hex_to_led_5_led_3[7:0]),
    .col29({8{1'b0}}), .col30(hex_to_led_5_led_4_4), .col31(hex_to_led_5_led_4_3),
    .col32(hex_to_led_5_led_4_2), .col33(hex_to_led_5_led_4));
  Multiplexer #(.width(3)) multiplexer_1 (
    .in0(INSTR[20:18]), .in1(INSTR[2:0]), .out(multiplexer_1_out), .sel(control_unit_1_reg2loc));
  branch_control branch_control_1 (
    .Z(alu_1_z), .CBR(control_unit_1_cbr), .PBR(control_unit_1_pbr), .ALUout(alu_1_aluout), .PC(PC_q),
    .IMMED12(INSTR[14:3]), .UBR(control_unit_1_ubr), .nextPC(out_1));
  DotMatrix #(.matrixcols(36), .matrixrows(8)) dotmatrix_6 (
    .col0(8'h42), .col1(8'h24), .col2(8'h18), .col3(8'h24), .col4(8'h42), .col5({8{1'b0}}), .col6(8'h70),
    .col7(8'h10), .col8(8'h10), .col9(8'h7e), .col10({8{1'b0}}), .col11(8'h24), .col12(8'h24), .col13(8'h24),
    .col14(8'h24), .col15(8'h24), .col16({8{1'b0}}), .col17(hex_to_led_6_led_1_4),
    .col18(hex_to_led_6_led_1_3), .col19(hex_to_led_6_led_1_2), .col20(hex_to_led_6_led_1),
    .col21({8{1'b0}}), .col22(hex_to_led_6_led_2_4), .col23(hex_to_led_6_led_2_3),
    .col24(hex_to_led_6_led_2_2), .col25(hex_to_led_6_led_2), .col26({8{1'b0}}),
    .col27(hex_to_led_6_led_3_4), .col28(hex_to_led_6_led_3_3), .col29(hex_to_led_6_led_3_2),
    .col30(hex_to_led_6_led_3), .col31({8{1'b0}}), .col32(hex_to_led_6_led_4_4),
    .col33(hex_to_led_6_led_4_3), .col34(hex_to_led_6_led_4_2), .col35(hex_to_led_6_led_4));
  DotMatrix #(.matrixcols(36), .matrixrows(8)) dotmatrix_7 (
    .col0(8'h42), .col1(8'h24), .col2(8'h18), .col3(8'h24), .col4(8'h42), .col5({8{1'b0}}), .col6(8'h72),
    .col7(8'h52), .col8(8'h52), .col9(8'h5e), .col10({8{1'b0}}), .col11(8'h24), .col12(8'h24), .col13(8'h24),
    .col14(8'h24), .col15(8'h24), .col16({8{1'b0}}), .col17(hex_to_led_7_led_1_4),
    .col18(hex_to_led_7_led_1_3), .col19(hex_to_led_7_led_1_2), .col20(hex_to_led_7_led_1),
    .col21({8{1'b0}}), .col22(hex_to_led_7_led_2_4), .col23(hex_to_led_7_led_2_3),
    .col24(hex_to_led_7_led_2_2), .col25(hex_to_led_7_led_2), .col26({8{1'b0}}),
    .col27(hex_to_led_7_led_3_4), .col28(hex_to_led_7_led_3_3), .col29(hex_to_led_7_led_3_2),
    .col30(hex_to_led_7_led_3), .col31({8{1'b0}}), .col32(hex_to_led_7_led_4_4),
    .col33(hex_to_led_7_led_4_3), .col34(hex_to_led_7_led_4_2), .col35(hex_to_led_7_led_4));
  DotMatrix #(.matrixcols(36), .matrixrows(8)) dotmatrix_8 (
    .col0({8{1'b0}}), .col1(8'h7e), .col2(8'h2), .col3(8'h2), .col4(8'h2), .col5({8{1'b0}}), .col6(8'h7e),
    .col7(8'h48), .col8(8'h54), .col9(8'h72), .col10({8{1'b0}}), .col11(8'h24), .col12(8'h24), .col13(8'h24),
    .col14(8'h24), .col15(8'h24), .col16({8{1'b0}}), .col17(hex_to_led_8_led_1_4),
    .col18(hex_to_led_8_led_1_3), .col19(hex_to_led_8_led_1_2), .col20(hex_to_led_8_led_1),
    .col21({8{1'b0}}), .col22(hex_to_led_8_led_2_4), .col23(hex_to_led_8_led_2_3),
    .col24(hex_to_led_8_led_2_2), .col25(hex_to_led_8_led_2), .col26({8{1'b0}}),
    .col27(hex_to_led_8_led_3_4), .col28(hex_to_led_8_led_3_3), .col29(hex_to_led_8_led_3_2),
    .col30(hex_to_led_8_led_3), .col31({8{1'b0}}), .col32(hex_to_led_8_led_4_4),
    .col33(hex_to_led_8_led_4_3), .col34(hex_to_led_8_led_4_2), .col35(hex_to_led_8_led_4));
  DotMatrix #(.matrixcols(36), .matrixrows(8)) dotmatrix_9 (
    .col0(8'h42), .col1(8'h24), .col2(8'h18), .col3(8'h24), .col4(8'h42), .col5({8{1'b0}}), .col6(8'h46),
    .col7(8'h4a), .col8(8'h52), .col9(8'h62), .col10({8{1'b0}}), .col11(8'h24), .col12(8'h24), .col13(8'h24),
    .col14(8'h24), .col15(8'h24), .col16({8{1'b0}}), .col17(hex_to_led_9_led_1_4),
    .col18(hex_to_led_9_led_1_3), .col19(hex_to_led_9_led_1_2), .col20(hex_to_led_9_led_1),
    .col21({8{1'b0}}), .col22(hex_to_led_9_led_2_4), .col23(hex_to_led_9_led_2_3),
    .col24(hex_to_led_9_led_2_2), .col25(hex_to_led_9_led_2), .col26({8{1'b0}}),
    .col27(hex_to_led_9_led_3_4), .col28(hex_to_led_9_led_3_3), .col29(hex_to_led_9_led_3_2),
    .col30(hex_to_led_9_led_3), .col31({8{1'b0}}), .col32(hex_to_led_9_led_4_4),
    .col33(hex_to_led_9_led_4_3), .col34(hex_to_led_9_led_4_2), .col35(hex_to_led_9_led_4));
  assign bit_extender_1_out = {{4{INSTR[14]}}, INSTR[14:3]};  // Bit_Extender bit_extender_1
  hex_to_LED hex_to_led_5 (
    .HEX_DIGIT(PC_q),
    .LED_4({hex_to_led_5_led_4_4, hex_to_led_5_led_4_3, hex_to_led_5_led_4_2, hex_to_led_5_led_4}),
    .LED_1({hex_to_led_5_led_1_4, hex_to_led_5_led_1_3, hex_to_led_5_led_1_2, hex_to_led_5_led_1}),
    .LED_2({hex_to_led_5_led_2_4, hex_to_led_5_led_2_3, hex_to_led_5_led_2_2, hex_to_led_5_led_2}),
    .LED_3(hex_to_led_5_led_3));
  register_file register_file_1 (
    .ReadReg1(INSTR[17:15]), .ReadReg2(multiplexer_1_out), .WriteToReg(INSTR[20:18]),
    .sysclock(SYS_CLOCK_out), .RegWriteSwitch(control_unit_1_regwrite), .RegDataW(out_2),
    .X3(register_file_1_x3), .XZR(register_file_1_xzr), .RegData1(register_file_1_regdata1),
    .RegData2(register_file_1_regdata2), .X0(register_file_1_x0), .X4(register_file_1_x4),
    .X1(register_file_1_x1), .X5(register_file_1_x5), .X2(register_file_1_x2), .LR(register_file_1_lr));
  Multiplexer #(.width(16)) multiplexer_2 (
    .in0(bit_extender_1_out), .in1(register_file_1_regdata2), .out(multiplexer_2_out),
    .sel(control_unit_1_alusrc));
  hex_to_LED hex_to_led_6 (
    .HEX_DIGIT(register_file_1_x4),
    .LED_4({hex_to_led_6_led_4_4, hex_to_led_6_led_4_3, hex_to_led_6_led_4_2, hex_to_led_6_led_4}),
    .LED_1({hex_to_led_6_led_1_4, hex_to_led_6_led_1_3, hex_to_led_6_led_1_2, hex_to_led_6_led_1}),
    .LED_2({hex_to_led_6_led_2_4, hex_to_led_6_led_2_3, hex_to_led_6_led_2_2, hex_to_led_6_led_2}),
    .LED_3({hex_to_led_6_led_3_4, hex_to_led_6_led_3_3, hex_to_led_6_led_3_2, hex_to_led_6_led_3}));
  hex_to_LED hex_to_led_7 (
    .HEX_DIGIT(register_file_1_x5),
    .LED_4({hex_to_led_7_led_4_4, hex_to_led_7_led_4_3, hex_to_led_7_led_4_2, hex_to_led_7_led_4}),
    .LED_1({hex_to_led_7_led_1_4, hex_to_led_7_led_1_3, hex_to_led_7_led_1_2, hex_to_led_7_led_1}),
    .LED_2({hex_to_led_7_led_2_4, hex_to_led_7_led_2_3, hex_to_led_7_led_2_2, hex_to_led_7_led_2}),
    .LED_3({hex_to_led_7_led_3_4, hex_to_led_7_led_3_3, hex_to_led_7_led_3_2, hex_to_led_7_led_3}));
  hex_to_LED hex_to_led_8 (
    .HEX_DIGIT(register_file_1_lr),
    .LED_4({hex_to_led_8_led_4_4, hex_to_led_8_led_4_3, hex_to_led_8_led_4_2, hex_to_led_8_led_4}),
    .LED_1({hex_to_led_8_led_1_4, hex_to_led_8_led_1_3, hex_to_led_8_led_1_2, hex_to_led_8_led_1}),
    .LED_2({hex_to_led_8_led_2_4, hex_to_led_8_led_2_3, hex_to_led_8_led_2_2, hex_to_led_8_led_2}),
    .LED_3({hex_to_led_8_led_3_4, hex_to_led_8_led_3_3, hex_to_led_8_led_3_2, hex_to_led_8_led_3}));
  hex_to_LED hex_to_led_9 (
    .HEX_DIGIT(register_file_1_xzr),
    .LED_4({hex_to_led_9_led_4_4, hex_to_led_9_led_4_3, hex_to_led_9_led_4_2, hex_to_led_9_led_4}),
    .LED_1({hex_to_led_9_led_1_4, hex_to_led_9_led_1_3, hex_to_led_9_led_1_2, hex_to_led_9_led_1}),
    .LED_2({hex_to_led_9_led_2_4, hex_to_led_9_led_2_3, hex_to_led_9_led_2_2, hex_to_led_9_led_2}),
    .LED_3({hex_to_led_9_led_3_4, hex_to_led_9_led_3_3, hex_to_led_9_led_3_2, hex_to_led_9_led_3}));
  RAM #(.addrWidth(16), .dataWidth(16), .enables("line"), .\type ("nonvolatile")) DATA_MEMORY (
    .addr(alu_1_aluout), .we(control_unit_1_memwrite), .clk(MEM_CLOCK_out), .din(register_file_1_regdata2),
    .dout(DATA_MEMORY_dout));
  Clock MEM_CLOCK (.out(MEM_CLOCK_out));
  ALU alu_1 (
    .inputA(register_file_1_regdata1), .inputB(multiplexer_2_out), .OPCODE(INSTR[23:21]),
    .ALUout(alu_1_aluout), .Z(alu_1_z));
  DotMatrix #(.matrixcols(20), .matrixrows(8)) dotmatrix_10 (
    .col0(instr_led_1_letter_1_4), .col1(instr_led_1_letter_1_3), .col2(instr_led_1_letter_1_2),
    .col3(instr_led_1_letter_1), .col4({8{1'b0}}), .col5(instr_led_1_letter_2_4),
    .col6(instr_led_1_letter_2_3), .col7(instr_led_1_letter_2_2), .col8(instr_led_1_letter_2),
    .col9({8{1'b0}}), .col10(instr_led_1_letter_3_4), .col11(instr_led_1_letter_3_3),
    .col12(instr_led_1_letter_3_2), .col13(instr_led_1_letter_3), .col14({8{1'b0}}),
    .col15(instr_led_1_letter_4_4), .col16(instr_led_1_letter_4_3), .col17(instr_led_1_letter_4_2),
    .col18(instr_led_1_letter_4), .col19({8{1'b0}}));
  Multiplexer #(.width(16)) multiplexer_3 (
    .in0(alu_1_aluout), .in1(DATA_MEMORY_dout), .out(multiplexer_3_out), .sel(control_unit_1_memtoreg));
  INSTR_LED instr_led_1 (
    .OPCODE(INSTR[23:21]),
    .Letter_4({instr_led_1_letter_4_4, instr_led_1_letter_4_3, instr_led_1_letter_4_2, instr_led_1_letter_4}),
    .Letter_1({instr_led_1_letter_1_4, instr_led_1_letter_1_3, instr_led_1_letter_1_2, instr_led_1_letter_1}),
    .Letter_2({instr_led_1_letter_2_4, instr_led_1_letter_2_3, instr_led_1_letter_2_2, instr_led_1_letter_2}),
    .Letter_3({instr_led_1_letter_3_4, instr_led_1_letter_3_3, instr_led_1_letter_3_2, instr_led_1_letter_3}));
  Multiplexer #(.width(16)) multiplexer_4 (
    .in0(multiplexer_3_out), .in1(adder_1_out), .out(out_2), .sel(control_unit_1_linkreg));
  Adder #(.width(16)) adder_1 (.a(PC_q), .b(16'h1), .out(adder_1_out));  // open: cin, cout

  // Notes on the sheet:
  //   2 Ticks long
  //   Name: The Death Machine
  //   Alexander Jansiewicz and Clare O'Brien
  //   I pledge my honor that I have abided by the Stevens Honor System.
  //   OPCODE
  //   TARGET
  //   OPRND1
  //   IMM12
  //   OPRND2
  //   1 Tick long
endmodule

module register_file (
  input  [15:0] RegDataW,
  input  sysclock,
  input  RegWriteSwitch,
  input  [2:0] ReadReg1,
  input  [2:0] ReadReg2,
  input  [2:0] WriteToReg,
  output [15:0] X0,
  output [15:0] X1,
  output [15:0] X2,
  output [15:0] X3,
  output [15:0] RegData1,
  output [15:0] RegData2,
  output [15:0] XZR,
  output [15:0] X4,
  output [15:0] X5,
  output [15:0] LR
);

  wire and_1_out, and_2_out, and_3_out, and_4_out, and_5_out, and_6_out, and_7_out, and_8_out,
       decoder_1_out0, decoder_1_out1, decoder_1_out2, decoder_1_out3, decoder_1_out4, decoder_1_out5,
       decoder_1_out6;

  Decoder #(.enable("false"), .select(3)) decoder_1 (
    .out0(decoder_1_out0), .out1(decoder_1_out1), .out2(decoder_1_out2), .out3(decoder_1_out3),
    .out4(decoder_1_out4), .out5(decoder_1_out5), .out6(decoder_1_out6), .out7(RegWriteSwitch),
    .sel(WriteToReg));
  Register #(.width(16)) REG_X0 (.D(RegDataW), .en(and_1_out), .clk(sysclock), .Q(X0));  // open: clr
  and and_1 (and_1_out, decoder_1_out0, RegWriteSwitch);
  Register #(.width(16)) REG_X4 (.D(RegDataW), .en(and_2_out), .clk(sysclock), .Q(X4));  // open: clr
  and and_2 (and_2_out, decoder_1_out4, RegWriteSwitch);
  Register #(.width(16)) REG_X1 (.D(RegDataW), .en(and_3_out), .clk(sysclock), .Q(X1));  // open: clr
  and and_3 (and_3_out, decoder_1_out1, RegWriteSwitch);
  Register #(.width(16)) REG_X5 (.D(RegDataW), .en(and_4_out), .clk(sysclock), .Q(X5));  // open: clr
  and and_4 (and_4_out, decoder_1_out5, RegWriteSwitch);
  Register #(.width(16)) REG_X2 (.D(RegDataW), .en(and_5_out), .clk(sysclock), .Q(X2));  // open: clr
  and and_5 (and_5_out, decoder_1_out2, RegWriteSwitch);
  Register #(.width(16)) REG_LINK (.D(RegDataW), .en(and_6_out), .clk(sysclock), .Q(LR));  // open: clr
  and and_6 (and_6_out, decoder_1_out6, RegWriteSwitch);
  Register #(.width(16)) REG_X3 (.D(RegDataW), .en(and_7_out), .clk(sysclock), .Q(X3));  // open: clr
  and and_7 (and_7_out, decoder_1_out3, RegWriteSwitch);
  Register #(.width(16)) REG_ZERO (.D({16{1'b0}}), .en(and_8_out), .clk(sysclock), .Q(XZR));  // open: clr
  and and_8 (and_8_out, RegWriteSwitch, RegWriteSwitch);
  Multiplexer #(.select(3), .width(16)) multiplexer_1 (
    .in0(X0), .in1(X1), .in2(X2), .in3(X3), .in4(X4), .in5(X5), .in6(LR), .in7(XZR), .out(RegData1),
    .sel(ReadReg1));
  Multiplexer #(.select(3), .width(16)) multiplexer_2 (
    .in0(X0), .in1(X1), .in2(X2), .in3(X3), .in4(X4), .in5(X5), .in6(LR), .in7(XZR), .out(RegData2),
    .sel(ReadReg2));

  // Notes on the sheet:
  //   I pledge my honor that I have abided by the Stevens Honor System
  //   Alexander Jansiewicz and Clare O'Brien
  //   Implementation of Register File adapted from Lab 8
  //   WriteReg = 3 Bits
  //   RegWrite = 1 Bit
  //   RegDataW = 16 Bits
  //   ReadReg1 = 3 Bit
  //   ReadReg2 = 3 Bit
endmodule

module control_unit (
  input  [2:0] OPCODE,
  output Reg2Loc,
  output RegWrite,
  output MemToReg,
  output MemWrite,
  output ALUsrc,
  output PBr,
  output CBr,
  output UBr,
  output LinkReg
);

  wire and_2_out, and_3_out, and_4_out, and_5_out, and_8_out, and_9_out, not_1_out, not_2_out, not_3_out,
       not_4_out, not_5_out, not_6_out, not_7_out, not_8_out, not_9_out, not_10_out, not_11_out, not_12_out,
       not_13_out, not_14_out, not_15_out, not_16_out, not_17_out, not_18_out, not_19_out, not_20_out;

  not not_1 (not_1_out, OPCODE[2]);
  not not_2 (not_2_out, OPCODE[1]);
  not not_3 (not_3_out, OPCODE[2]);
  not not_4 (not_4_out, OPCODE[1]);
  not not_5 (not_5_out, OPCODE[0]);
  not not_6 (not_6_out, OPCODE[2]);
  not not_7 (not_7_out, OPCODE[1]);
  not not_8 (not_8_out, OPCODE[2]);
  not not_9 (not_9_out, OPCODE[0]);
  not not_10 (not_10_out, OPCODE[1]);
  not not_11 (not_11_out, OPCODE[0]);
  not not_12 (not_12_out, OPCODE[2]);
  not not_13 (not_13_out, OPCODE[0]);
  not not_14 (not_14_out, OPCODE[2]);
  not not_15 (not_15_out, OPCODE[2]);
  not not_16 (not_16_out, OPCODE[0]);
  not not_17 (not_17_out, OPCODE[2]);
  not not_18 (not_18_out, OPCODE[1]);
  not not_19 (not_19_out, OPCODE[1]);
  not not_20 (not_20_out, OPCODE[0]);
  and and_1 (Reg2Loc, not_1_out, not_2_out);
  and and_2 (and_2_out, not_3_out, not_4_out, not_5_out);
  and and_3 (and_3_out, not_6_out, not_7_out, OPCODE[0]);
  and and_4 (and_4_out, not_8_out, OPCODE[1], not_9_out);
  and and_5 (and_5_out, OPCODE[2], not_10_out, not_11_out);
  and and_6 (MemToReg, not_12_out, OPCODE[1], not_13_out);
  and and_7 (MemWrite, not_14_out, OPCODE[1], OPCODE[0]);
  and and_8 (and_8_out, not_15_out, OPCODE[1], not_16_out);
  and and_9 (and_9_out, not_17_out, OPCODE[1], OPCODE[0]);
  and and_10 (PBr, OPCODE[2], not_18_out, OPCODE[0]);
  and and_11 (CBr, OPCODE[2], OPCODE[1]);
  and and_12 (LinkReg, OPCODE[2], not_19_out, not_20_out);
  or or_1 (RegWrite, and_2_out, and_3_out, and_4_out, and_5_out);
  nor nor_1 (ALUsrc, and_8_out, and_9_out);

  assign UBr = LinkReg;

  // Notes on the sheet:
  //   I pledge my honor that I have abided by the Stevens Honor System
  //   Alexander Jansiewicz and Clare O'Brien
endmodule

module ALU (
  input  [15:0] inputA,
  input  [15:0] inputB,
  input  [2:0] OPCODE,
  output [15:0] ALUout,
  output Z
);

  wire and_1_out, and_2_out, comparator_1_eq, multiplexer_3_out, not_1_out, not_2_out, not_3_out;
  wire [15:0] adder_1_out, multiplexer_1_out, subtractor_1_out;

  not not_1 (not_1_out, OPCODE[2]);
  not not_2 (not_2_out, OPCODE[1]);
  Adder #(.width(16)) adder_1 (.a(inputA), .b(inputB), .out(adder_1_out));  // open: cin, cout
  Multiplexer #(.width(16)) multiplexer_1 (
    .in0(adder_1_out), .in1(subtractor_1_out), .out(multiplexer_1_out), .sel(and_1_out));
  Subtractor #(.width(16)) subtractor_1 (.a(inputA), .b(inputB), .out(subtractor_1_out));  // open: bin, bout
  and and_1 (and_1_out, not_1_out, not_2_out, OPCODE[0]);
  Multiplexer #(.width(16)) multiplexer_2 (.in0(multiplexer_1_out), .in1(inputB), .out(ALUout), .sel(OPCODE[2]));
  Comparator #(.width(16)) comparator_1 (.a(inputB), .b({16{1'b0}}), .eq(comparator_1_eq));  // open: gt, lt
  and and_2 (and_2_out, OPCODE[2], OPCODE[1]);
  Multiplexer multiplexer_3 (.in0(comparator_1_eq), .in1(not_3_out), .out(multiplexer_3_out), .sel(OPCODE[0]));
  not not_3 (not_3_out, comparator_1_eq);
  Multiplexer multiplexer_4 (.in0(1'b0), .in1(multiplexer_3_out), .out(Z), .sel(and_2_out));

  // Notes on the sheet:
  //   I pledge my honor that I have abided by the Stevens Honor System
  //   Alexander Jansiewicz and Clare O'Brien
endmodule

module branch_control (
  input  Z,
  input  CBR,
  input  UBR,
  input  PBR,
  input  [15:0] ALUout,
  input  [15:0] PC,
  input  [11:0] IMMED12,
  output [15:0] nextPC
);

  wire and_1_out, or_1_out;
  wire [15:0] adder_1_out, adder_2_out, bit_extender_1_out, multiplexer_1_out;

  and and_1 (and_1_out, Z, CBR);
  assign bit_extender_1_out = {{4{IMMED12[11]}}, IMMED12};  // Bit_Extender bit_extender_1
  or or_1 (or_1_out, and_1_out, UBR);
  Adder #(.width(16)) adder_1 (.a(PC), .b(bit_extender_1_out), .out(adder_1_out));  // open: cin, cout
  Adder #(.width(16)) adder_2 (.a(PC), .b(16'h1), .out(adder_2_out));  // open: cin, cout
  Multiplexer #(.width(16)) multiplexer_1 (
    .in0(adder_2_out), .in1(adder_1_out), .out(multiplexer_1_out), .sel(or_1_out));
  Multiplexer #(.width(16)) multiplexer_2 (.in0(multiplexer_1_out), .in1(ALUout), .out(nextPC), .sel(PBR));

  // Notes on the sheet:
  //   I pledge my honor that I have abided by the Stevens Honor System
  //   Alexander Jansiewicz and Clare O'Brien
  //   BrPC
  //   PC + 1
  //   Br
  //   if PBr: PC = ALUout else: (PC = BrPC if Br else nextPC)
endmodule

module display (
);

  wire [7:0] hex_to_led_1_led_1, hex_to_led_1_led_1_2, hex_to_led_1_led_1_3, hex_to_led_1_led_1_4,
       hex_to_led_1_led_2, hex_to_led_1_led_2_2, hex_to_led_1_led_2_3, hex_to_led_1_led_2_4,
       hex_to_led_1_led_3, hex_to_led_1_led_3_2, hex_to_led_1_led_3_3, hex_to_led_1_led_3_4,
       hex_to_led_1_led_4, hex_to_led_1_led_4_2, hex_to_led_1_led_4_3, hex_to_led_1_led_4_4,
       hex_to_led_2_led_1, hex_to_led_2_led_1_2, hex_to_led_2_led_1_3, hex_to_led_2_led_1_4,
       hex_to_led_2_led_2, hex_to_led_2_led_2_2, hex_to_led_2_led_2_3, hex_to_led_2_led_2_4,
       hex_to_led_2_led_3, hex_to_led_2_led_3_2, hex_to_led_2_led_3_3, hex_to_led_2_led_3_4,
       hex_to_led_2_led_4, hex_to_led_2_led_4_2, hex_to_led_2_led_4_3, hex_to_led_2_led_4_4,
       hex_to_led_3_led_1, hex_to_led_3_led_1_2, hex_to_led_3_led_1_3, hex_to_led_3_led_1_4,
       hex_to_led_3_led_2, hex_to_led_3_led_2_2, hex_to_led_3_led_2_3, hex_to_led_3_led_2_4,
       hex_to_led_3_led_3, hex_to_led_3_led_3_2, hex_to_led_3_led_3_3, hex_to_led_3_led_3_4,
       hex_to_led_3_led_4, hex_to_led_3_led_4_2, hex_to_led_3_led_4_3, hex_to_led_3_led_4_4,
       hex_to_led_4_led_1, hex_to_led_4_led_1_2, hex_to_led_4_led_1_3, hex_to_led_4_led_1_4,
       hex_to_led_4_led_2, hex_to_led_4_led_2_2, hex_to_led_4_led_2_3, hex_to_led_4_led_2_4,
       hex_to_led_4_led_3, hex_to_led_4_led_3_2, hex_to_led_4_led_3_3, hex_to_led_4_led_3_4,
       hex_to_led_4_led_4, hex_to_led_4_led_4_2, hex_to_led_4_led_4_3, hex_to_led_4_led_4_4,
       hex_to_led_5_led_1, hex_to_led_5_led_1_2, hex_to_led_5_led_1_3, hex_to_led_5_led_1_4,
       hex_to_led_5_led_2, hex_to_led_5_led_2_2, hex_to_led_5_led_2_3, hex_to_led_5_led_2_4, undriven;
  wire [15:0] bit_extender_1_out;

  DotMatrix #(.matrixcols(36), .matrixrows(8)) dotmatrix_1 (
    .col0(8'h42), .col1(8'h24), .col2(8'h18), .col3(8'h24), .col4(8'h42), .col5({8{1'b0}}), .col6(8'h7e),
    .col7(8'h42), .col8(8'h42), .col9(8'h7e), .col10({8{1'b0}}), .col11(8'h24), .col12(8'h24), .col13(8'h24),
    .col14(8'h24), .col15(8'h24), .col16({8{1'b0}}), .col17(hex_to_led_1_led_1_4),
    .col18(hex_to_led_1_led_1_3), .col19(hex_to_led_1_led_1_2), .col20(hex_to_led_1_led_1),
    .col21({8{1'b0}}), .col22(hex_to_led_1_led_2_4), .col23(hex_to_led_1_led_2_3),
    .col24(hex_to_led_1_led_2_2), .col25(hex_to_led_1_led_2), .col26({8{1'b0}}),
    .col27(hex_to_led_1_led_3_4), .col28(hex_to_led_1_led_3_3), .col29(hex_to_led_1_led_3_2),
    .col30(hex_to_led_1_led_3), .col31({8{1'b0}}), .col32(hex_to_led_1_led_4_4),
    .col33(hex_to_led_1_led_4_3), .col34(hex_to_led_1_led_4_2), .col35(hex_to_led_1_led_4));
  DotMatrix #(.matrixcols(36), .matrixrows(8)) dotmatrix_2 (
    .col0(8'h42), .col1(8'h24), .col2(8'h18), .col3(8'h24), .col4(8'h42), .col5({8{1'b0}}), .col6({8{1'b0}}),
    .col7(8'h7e), .col8({8{1'b0}}), .col9({8{1'b0}}), .col10({8{1'b0}}), .col11(8'h24), .col12(8'h24),
    .col13(8'h24), .col14(8'h24), .col15(8'h24), .col16({8{1'b0}}), .col17(hex_to_led_2_led_1_4),
    .col18(hex_to_led_2_led_1_3), .col19(hex_to_led_2_led_1_2), .col20(hex_to_led_2_led_1),
    .col21({8{1'b0}}), .col22(hex_to_led_2_led_2_4), .col23(hex_to_led_2_led_2_3),
    .col24(hex_to_led_2_led_2_2), .col25(hex_to_led_2_led_2), .col26({8{1'b0}}),
    .col27(hex_to_led_2_led_3_4), .col28(hex_to_led_2_led_3_3), .col29(hex_to_led_2_led_3_2),
    .col30(hex_to_led_2_led_3), .col31({8{1'b0}}), .col32(hex_to_led_2_led_4_4),
    .col33(hex_to_led_2_led_4_3), .col34(hex_to_led_2_led_4_2), .col35(hex_to_led_2_led_4));
  DotMatrix #(.matrixcols(36), .matrixrows(8)) dotmatrix_3 (
    .col0(8'h42), .col1(8'h24), .col2(8'h18), .col3(8'h24), .col4(8'h42), .col5({8{1'b0}}), .col6(8'h4e),
    .col7(8'h4a), .col8(8'h4a), .col9(8'h7a), .col10({8{1'b0}}), .col11(8'h24), .col12(8'h24), .col13(8'h24),
    .col14(8'h24), .col15(8'h24), .col16({8{1'b0}}), .col17(hex_to_led_3_led_1_4),
    .col18(hex_to_led_3_led_1_3), .col19(hex_to_led_3_led_1_2), .col20(hex_to_led_3_led_1),
    .col21({8{1'b0}}), .col22(hex_to_led_3_led_2_4), .col23(hex_to_led_3_led_2_3),
    .col24(hex_to_led_3_led_2_2), .col25(hex_to_led_3_led_2), .col26({8{1'b0}}),
    .col27(hex_to_led_3_led_3_4), .col28(hex_to_led_3_led_3_3), .col29(hex_to_led_3_led_3_2),
    .col30(hex_to_led_3_led_3), .col31({8{1'b0}}), .col32(hex_to_led_3_led_4_4),
    .col33(hex_to_led_3_led_4_3), .col34(hex_to_led_3_led_4_2), .col35(hex_to_led_3_led_4));
  DotMatrix #(.matrixcols(36), .matrixrows(8)) dotmatrix_4 (
    .col0(8'h42), .col1(8'h24), .col2(8'h18), .col3(8'h24), .col4(8'h42), .col5({8{1'b0}}), .col6(8'h4a),
    .col7(8'h4a), .col8(8'h4a), .col9(8'h7e), .col10({8{1'b0}}), .col11(8'h24), .col12(8'h24), .col13(8'h24),
    .col14(8'h24), .col15(8'h24), .col16({8{1'b0}}), .col17(hex_to_led_4_led_1_4),
    .col18(hex_to_led_4_led_1_3), .col19(hex_to_led_4_led_1_2), .col20(hex_to_led_4_led_1),
    .col21({8{1'b0}}), .col22(hex_to_led_4_led_2_4), .col23(hex_to_led_4_led_2_3),
    .col24(hex_to_led_4_led_2_2), .col25(hex_to_led_4_led_2), .col26({8{1'b0}}),
    .col27(hex_to_led_4_led_3_4), .col28(hex_to_led_4_led_3_3), .col29(hex_to_led_4_led_3_2),
    .col30(hex_to_led_4_led_3), .col31({8{1'b0}}), .col32(hex_to_led_4_led_4_4),
    .col33(hex_to_led_4_led_4_3), .col34(hex_to_led_4_led_4_2), .col35(hex_to_led_4_led_4));
  hex_to_LED hex_to_led_1 (
    .HEX_DIGIT(16'h123),
    .LED_4({hex_to_led_1_led_4_4, hex_to_led_1_led_4_3, hex_to_led_1_led_4_2, hex_to_led_1_led_4}),
    .LED_1({hex_to_led_1_led_1_4, hex_to_led_1_led_1_3, hex_to_led_1_led_1_2, hex_to_led_1_led_1}),
    .LED_2({hex_to_led_1_led_2_4, hex_to_led_1_led_2_3, hex_to_led_1_led_2_2, hex_to_led_1_led_2}),
    .LED_3({hex_to_led_1_led_3_4, hex_to_led_1_led_3_3, hex_to_led_1_led_3_2, hex_to_led_1_led_3}));
  hex_to_LED hex_to_led_2 (
    .HEX_DIGIT(16'h4567),
    .LED_4({hex_to_led_2_led_4_4, hex_to_led_2_led_4_3, hex_to_led_2_led_4_2, hex_to_led_2_led_4}),
    .LED_1({hex_to_led_2_led_1_4, hex_to_led_2_led_1_3, hex_to_led_2_led_1_2, hex_to_led_2_led_1}),
    .LED_2({hex_to_led_2_led_2_4, hex_to_led_2_led_2_3, hex_to_led_2_led_2_2, hex_to_led_2_led_2}),
    .LED_3({hex_to_led_2_led_3_4, hex_to_led_2_led_3_3, hex_to_led_2_led_3_2, hex_to_led_2_led_3}));
  hex_to_LED hex_to_led_3 (
    .HEX_DIGIT(16'h89ab),
    .LED_4({hex_to_led_3_led_4_4, hex_to_led_3_led_4_3, hex_to_led_3_led_4_2, hex_to_led_3_led_4}),
    .LED_1({hex_to_led_3_led_1_4, hex_to_led_3_led_1_3, hex_to_led_3_led_1_2, hex_to_led_3_led_1}),
    .LED_2({hex_to_led_3_led_2_4, hex_to_led_3_led_2_3, hex_to_led_3_led_2_2, hex_to_led_3_led_2}),
    .LED_3({hex_to_led_3_led_3_4, hex_to_led_3_led_3_3, hex_to_led_3_led_3_2, hex_to_led_3_led_3}));
  hex_to_LED hex_to_led_4 (
    .HEX_DIGIT(16'hcdef),
    .LED_4({hex_to_led_4_led_4_4, hex_to_led_4_led_4_3, hex_to_led_4_led_4_2, hex_to_led_4_led_4}),
    .LED_1({hex_to_led_4_led_1_4, hex_to_led_4_led_1_3, hex_to_led_4_led_1_2, hex_to_led_4_led_1}),
    .LED_2({hex_to_led_4_led_2_4, hex_to_led_4_led_2_3, hex_to_led_4_led_2_2, hex_to_led_4_led_2}),
    .LED_3({hex_to_led_4_led_3_4, hex_to_led_4_led_3_3, hex_to_led_4_led_3_2, hex_to_led_4_led_3}));
  DotMatrix #(.matrixcols(24), .matrixrows(8)) dotmatrix_5 (
    .col0(8'h7e), .col1(8'h50), .col2(8'h50), .col3(8'h70), .col4({8{1'b0}}), .col5(8'h7e), .col6(8'h42),
    .col7(8'h42), .col8(8'h42), .col9({8{1'b0}}), .col10(8'h24), .col11(8'h24), .col12(8'h24), .col13(8'h24),
    .col14({8{1'b0}}), .col15(hex_to_led_5_led_1_4), .col16(hex_to_led_5_led_1_3),
    .col17(hex_to_led_5_led_1_2), .col18(hex_to_led_5_led_1), .col19({8{1'b0}}),
    .col20(hex_to_led_5_led_2_4), .col21(hex_to_led_5_led_2_3), .col22(hex_to_led_5_led_2_2),
    .col23(hex_to_led_5_led_2));
  hex_to_LED hex_to_led_5 (
    .HEX_DIGIT(bit_extender_1_out),
    .LED_1({hex_to_led_5_led_1_4, hex_to_led_5_led_1_3, hex_to_led_5_led_1_2, hex_to_led_5_led_1}),
    .LED_2({hex_to_led_5_led_2_4, hex_to_led_5_led_2_3, hex_to_led_5_led_2_2, hex_to_led_5_led_2}));  // open: LED_4, LED_3
  assign bit_extender_1_out = {{8{undriven[7]}}, undriven};  // Bit_Extender bit_extender_1

  // Notes on the sheet:
  //   I pledge my honor that I have abided by the Stevens Honor System
  //   Alexander Jansiewicz and Clare O'Brien
endmodule

module hex_to_LED (
  input  [15:0] HEX_DIGIT,
  output [31:0] LED_1,
  output [31:0] LED_2,
  output [31:0] LED_3,
  output [31:0] LED_4
);

  DotMatrix #(.matrixcols(4), .matrixrows(8)) dotmatrix_1 (
    .col0(LED_1[31:24]), .col1(LED_1[23:16]), .col2(LED_1[15:8]), .col3(LED_1[7:0]));
  Multiplexer #(.select(4), .width(32)) multiplexer_1 (
    .in0(32'h7e42427e), .in1(32'h7e00), .in2(32'h5e525272), .in3(32'h5252527e), .in4(32'h7010107e),
    .in5(32'h7252525e), .in6(32'h7e52525e), .in7(32'h4040407e), .in8(32'h7e52527e), .in9(32'h7252527e),
    .in10(32'he0a0a0f), .in11(32'h7e0a0a0e), .in12(32'he0a0a0a), .in13(32'he0a0a7e), .in14(32'h1f15151d),
    .in15(32'h107e5050), .out(LED_1), .sel(HEX_DIGIT[15:12]));
  DotMatrix #(.matrixcols(4), .matrixrows(8)) dotmatrix_2 (
    .col0(LED_2[31:24]), .col1(LED_2[23:16]), .col2(LED_2[15:8]), .col3(LED_2[7:0]));
  Multiplexer #(.select(4), .width(32)) multiplexer_2 (
    .in0(32'h7e42427e), .in1(32'h7e00), .in2(32'h5e525272), .in3(32'h5252527e), .in4(32'h7010107e),
    .in5(32'h7252525e), .in6(32'h7e52525e), .in7(32'h4040407e), .in8(32'h7e52527e), .in9(32'h7252527e),
    .in10(32'he0a0a0f), .in11(32'h7e0a0a0e), .in12(32'he0a0a0a), .in13(32'he0a0a7e), .in14(32'h1f15151d),
    .in15(32'h107e5050), .out(LED_2), .sel(HEX_DIGIT[11:8]));
  DotMatrix #(.matrixcols(4), .matrixrows(8)) dotmatrix_3 (
    .col0(LED_3[31:24]), .col1(LED_3[23:16]), .col2(LED_3[15:8]), .col3(LED_3[7:0]));
  Multiplexer #(.select(4), .width(32)) multiplexer_3 (
    .in0(32'h7e42427e), .in1(32'h7e00), .in2(32'h5e525272), .in3(32'h5252527e), .in4(32'h7010107e),
    .in5(32'h7252525e), .in6(32'h7e52525e), .in7(32'h4040407e), .in8(32'h7e52527e), .in9(32'h7252527e),
    .in10(32'he0a0a0f), .in11(32'h7e0a0a0e), .in12(32'he0a0a0a), .in13(32'he0a0a7e), .in14(32'h1f15151d),
    .in15(32'h107e5050), .out(LED_3), .sel(HEX_DIGIT[7:4]));
  DotMatrix #(.matrixcols(4), .matrixrows(8)) dotmatrix_4 (
    .col0(LED_4[31:24]), .col1(LED_4[23:16]), .col2(LED_4[15:8]), .col3(LED_4[7:0]));
  Multiplexer #(.select(4), .width(32)) multiplexer_4 (
    .in0(32'h7e42427e), .in1(32'h7e00), .in2(32'h5e525272), .in3(32'h5252527e), .in4(32'h7010107e),
    .in5(32'h7252525e), .in6(32'h7e52525e), .in7(32'h4040407e), .in8(32'h7e52527e), .in9(32'h7252527e),
    .in10(32'he0a0a0f), .in11(32'h7e0a0a0e), .in12(32'he0a0a0a), .in13(32'he0a0a7e), .in14(32'h1f15151d),
    .in15(32'h107e5050), .out(LED_4), .sel(HEX_DIGIT[3:0]));

  // Notes on the sheet:
  //   I pledge my honor that I have abided by the Stevens Honor System
  //   Alexander Jansiewicz and Clare O'Brien
endmodule

module hex_to_LED_8bit (
  input  [7:0] HEX_DIGIT,
  output [31:0] LED_1,
  output [31:0] LED_2
);

  DotMatrix #(.matrixcols(4), .matrixrows(8)) dotmatrix_1 (
    .col0(LED_1[31:24]), .col1(LED_1[23:16]), .col2(LED_1[15:8]), .col3(LED_1[7:0]));
  Multiplexer #(.select(4), .width(32)) multiplexer_1 (
    .in0(32'h7e42427e), .in1(32'h7e00), .in2(32'h5e525272), .in3(32'h5252527e), .in4(32'h7010107e),
    .in5(32'h7252525e), .in6(32'h7e52525e), .in7(32'h4040407e), .in8(32'h7e52527e), .in9(32'h7252527e),
    .in10(32'he0a0a0f), .in11(32'h7e0a0a0e), .in12(32'he0a0a0a), .in13(32'he0a0a7e), .in14(32'h1f15151d),
    .in15(32'h107e5050), .out(LED_1), .sel(HEX_DIGIT[7:4]));
  DotMatrix #(.matrixcols(4), .matrixrows(8)) dotmatrix_2 (
    .col0(LED_2[31:24]), .col1(LED_2[23:16]), .col2(LED_2[15:8]), .col3(LED_2[7:0]));
  Multiplexer #(.select(4), .width(32)) multiplexer_2 (
    .in0(32'h7e42427e), .in1(32'h7e00), .in2(32'h5e525272), .in3(32'h5252527e), .in4(32'h7010107e),
    .in5(32'h7252525e), .in6(32'h7e52525e), .in7(32'h4040407e), .in8(32'h7e52527e), .in9(32'h7252527e),
    .in10(32'he0a0a0f), .in11(32'h7e0a0a0e), .in12(32'he0a0a0a), .in13(32'he0a0a7e), .in14(32'h1f15151d),
    .in15(32'h107e5050), .out(LED_2), .sel(HEX_DIGIT[3:0]));

  // Notes on the sheet:
  //   I pledge my honor that I have abided by the Stevens Honor System
  //   Alexander Jansiewicz and Clare O'Brien
endmodule

module INSTR_LED (
  input  [2:0] OPCODE,
  output [31:0] Letter_1,
  output [31:0] Letter_2,
  output [31:0] Letter_3,
  output [31:0] Letter_4
);

  DotMatrix #(.matrixcols(20), .matrixrows(8)) dotmatrix_1 (
    .col0(Letter_1[31:24]), .col1(Letter_1[23:16]), .col2(Letter_1[15:8]), .col3(Letter_1[7:0]),
    .col4({8{1'b0}}), .col5(Letter_2[31:24]), .col6(Letter_2[23:16]), .col7(Letter_2[15:8]),
    .col8(Letter_2[7:0]), .col9({8{1'b0}}), .col10(Letter_3[31:24]), .col11(Letter_3[23:16]),
    .col12(Letter_3[15:8]), .col13(Letter_3[7:0]), .col14({8{1'b0}}), .col15(Letter_4[31:24]),
    .col16(Letter_4[23:16]), .col17(Letter_4[15:8]), .col18(Letter_4[7:0]), .col19({8{1'b0}}));
  Multiplexer #(.select(3), .width(32)) multiplexer_1 (
    .in0(32'h7e48487e), .in1(32'h22524a44), .in2(32'h7e020202), .in3(32'h22524a44), .in4(32'h7e52320c),
    .in5(32'h7e485472), .in6(32'h3c424242), .in7(32'h3c424242), .out(Letter_1), .sel(OPCODE));
  Multiplexer #(.select(3), .width(32)) multiplexer_2 (
    .in0(32'h7e42423c), .in1(32'h7c02027c), .in2(32'h7e42423c), .in3(32'h407e7e40), .in4(32'h7e020202),
    .in5(32'h7e5a5a5a), .in6(32'h7e52320c), .in7(32'h7e52320c), .out(Letter_2), .sel(OPCODE));
  Multiplexer #(.select(3), .width(32)) multiplexer_3 (
    .in0(32'h7e42423c), .in1(32'h7e52320c), .in2(32'h7e485472), .in3(32'h7e485472), .in4({32{1'b0}}),
    .in5(32'h407e7e40), .in6(32'h464a5262), .in7(32'h7e381c7e), .out(Letter_3), .sel(OPCODE));
  Multiplexer #(.select(3), .width(32)) multiplexer_4 (
    .in0({32{1'b0}}), .in1({32{1'b0}}), .in2({32{1'b0}}), .in3({32{1'b0}}), .in4({32{1'b0}}),
    .in5({32{1'b0}}), .in6({32{1'b0}}), .in7(32'h464a5262), .out(Letter_4), .sel(OPCODE));

  // Notes on the sheet:
  //   I pledge my honor that I have abided by the Stevens Honor System
  //   Alexander Jansiewicz and Clare O'Brien
endmodule
